// Logisim project TicketsMachine.circ as structural Verilog
module main (
  input  in_1,
  input  in_2,
  input  [2:0] in_3,
  input  [2:0] in_4,
  input  [5:0] in_5,
  input  [7:0] in_6,
  input  [6:0] in_7,
  output [7:0] out_8,
  output [7:0] out_9,
  output [7:0] out_10,
  output [7:0] out_11,
  output [7:0] out_12,
  output [7:0] out_13,
  output [7:0] out_14,
  output out_15,
  output [6:0] out_16
);

  wire button_1_out, button_2_out, button_3_out, button_4_out, calculate_cost_1_error, calculate_rest_1_ok2,
       introduce_money_1_ok, memory_money_1_error, memory_tickets_1_error, procesare_rest_1_ok2;
  wire [3:0] number_splitter_1_hundreds_out, number_splitter_1_tens_out, number_splitter_1_units_out,
       number_splitter_2_hundreds_out, number_splitter_2_tens_out, number_splitter_2_units_out,
       number_splitter_3_hundreds_out, number_splitter_3_tens_out, number_splitter_3_units_out;
  wire [6:0] calculate_cost_1_data_out, calculate_rest_1_rest, hex_7seg_1_a_b_c_d_e_f_g,
       hex_7seg_2_a_b_c_d_e_f_g, hex_7seg_3_a_b_c_d_e_f_g, hex_7seg_4_a_b_c_d_e_f_g,
       hex_7seg_5_a_b_c_d_e_f_g, hex_7seg_6_a_b_c_d_e_f_g, hex_7seg_7_a_b_c_d_e_f_g,
       hex_7seg_8_a_b_c_d_e_f_g, hex_7seg_9_a_b_c_d_e_f_g, introduce_money_1_suma_ceruta,
       introduce_money_1_suma_data, procesare_rest_1_cinci, procesare_rest_1_czeci, procesare_rest_1_doi,
       procesare_rest_1_dzeci, procesare_rest_1_unu, procesare_rest_1_zece;

  Button button_1 (.out(button_1_out));
  number_splitter number_splitter_1 (
    .num_in(calculate_cost_1_data_out), .units_out(number_splitter_1_units_out),
    .tens_out(number_splitter_1_tens_out), .hundreds_out(number_splitter_1_hundreds_out));
  calculate_cost calculate_cost_1 (
    .button(button_1_out), .data_in(in_5), .data_out(calculate_cost_1_data_out),
    .error(calculate_cost_1_error));
  LED led_1 (.in(calculate_cost_1_error));
  number_splitter number_splitter_2 (
    .num_in(introduce_money_1_suma_data), .units_out(number_splitter_2_units_out),
    .tens_out(number_splitter_2_tens_out), .hundreds_out(number_splitter_2_hundreds_out));
  Button button_2 (.out(button_2_out));
  hex_7seg hex_7seg_1 (.hex_in(number_splitter_2_tens_out), .a_b_c_d_e_f_g(hex_7seg_1_a_b_c_d_e_f_g));
  hex_7seg hex_7seg_2 (.hex_in(number_splitter_2_units_out), .a_b_c_d_e_f_g(hex_7seg_2_a_b_c_d_e_f_g));
  hex_7seg hex_7seg_3 (.hex_in(number_splitter_1_tens_out), .a_b_c_d_e_f_g(hex_7seg_3_a_b_c_d_e_f_g));
  hex_7seg hex_7seg_4 (.hex_in(number_splitter_1_units_out), .a_b_c_d_e_f_g(hex_7seg_4_a_b_c_d_e_f_g));
  hex_7seg hex_7seg_5 (.hex_in(number_splitter_2_hundreds_out), .a_b_c_d_e_f_g(hex_7seg_5_a_b_c_d_e_f_g));
  hex_7seg hex_7seg_6 (.hex_in(number_splitter_1_hundreds_out), .a_b_c_d_e_f_g(hex_7seg_6_a_b_c_d_e_f_g));
  _7_Segment_Display #(.decimalPoint("false")) u_7_segment_display_1 (
    .g(hex_7seg_5_a_b_c_d_e_f_g[0]), .f(hex_7seg_5_a_b_c_d_e_f_g[1]), .a(hex_7seg_5_a_b_c_d_e_f_g[6]),
    .b(hex_7seg_5_a_b_c_d_e_f_g[5]), .e(hex_7seg_5_a_b_c_d_e_f_g[2]), .d(hex_7seg_5_a_b_c_d_e_f_g[3]),
    .c(hex_7seg_5_a_b_c_d_e_f_g[4]));
  _7_Segment_Display #(.decimalPoint("false")) u_7_segment_display_2 (
    .g(hex_7seg_6_a_b_c_d_e_f_g[0]), .f(hex_7seg_6_a_b_c_d_e_f_g[1]), .a(hex_7seg_6_a_b_c_d_e_f_g[6]),
    .b(hex_7seg_6_a_b_c_d_e_f_g[5]), .e(hex_7seg_6_a_b_c_d_e_f_g[2]), .d(hex_7seg_6_a_b_c_d_e_f_g[3]),
    .c(hex_7seg_6_a_b_c_d_e_f_g[4]));
  introduce_money introduce_money_1 (
    .cost(calculate_cost_1_data_out), .button(button_2_out), .addr(in_4),
    .suma_data(introduce_money_1_suma_data), .suma_ceruta(introduce_money_1_suma_ceruta),
    .ok(introduce_money_1_ok));
  _7_Segment_Display #(.decimalPoint("false")) u_7_segment_display_3 (
    .g(hex_7seg_1_a_b_c_d_e_f_g[0]), .f(hex_7seg_1_a_b_c_d_e_f_g[1]), .a(hex_7seg_1_a_b_c_d_e_f_g[6]),
    .b(hex_7seg_1_a_b_c_d_e_f_g[5]), .e(hex_7seg_1_a_b_c_d_e_f_g[2]), .d(hex_7seg_1_a_b_c_d_e_f_g[3]),
    .c(hex_7seg_1_a_b_c_d_e_f_g[4]));
  _7_Segment_Display #(.decimalPoint("false")) u_7_segment_display_4 (
    .g(hex_7seg_3_a_b_c_d_e_f_g[0]), .f(hex_7seg_3_a_b_c_d_e_f_g[1]), .a(hex_7seg_3_a_b_c_d_e_f_g[6]),
    .b(hex_7seg_3_a_b_c_d_e_f_g[5]), .e(hex_7seg_3_a_b_c_d_e_f_g[2]), .d(hex_7seg_3_a_b_c_d_e_f_g[3]),
    .c(hex_7seg_3_a_b_c_d_e_f_g[4]));
  _7_Segment_Display #(.decimalPoint("false")) u_7_segment_display_5 (
    .g(hex_7seg_2_a_b_c_d_e_f_g[0]), .f(hex_7seg_2_a_b_c_d_e_f_g[1]), .a(hex_7seg_2_a_b_c_d_e_f_g[6]),
    .b(hex_7seg_2_a_b_c_d_e_f_g[5]), .e(hex_7seg_2_a_b_c_d_e_f_g[2]), .d(hex_7seg_2_a_b_c_d_e_f_g[3]),
    .c(hex_7seg_2_a_b_c_d_e_f_g[4]));
  _7_Segment_Display #(.decimalPoint("false")) u_7_segment_display_6 (
    .g(hex_7seg_4_a_b_c_d_e_f_g[0]), .f(hex_7seg_4_a_b_c_d_e_f_g[1]), .a(hex_7seg_4_a_b_c_d_e_f_g[6]),
    .b(hex_7seg_4_a_b_c_d_e_f_g[5]), .e(hex_7seg_4_a_b_c_d_e_f_g[2]), .d(hex_7seg_4_a_b_c_d_e_f_g[3]),
    .c(hex_7seg_4_a_b_c_d_e_f_g[4]));
  calculate_rest calculate_rest_1 (
    .suma_data(introduce_money_1_suma_data), .suma_ceruta(introduce_money_1_suma_ceruta),
    .ok(introduce_money_1_ok), .rest(calculate_rest_1_rest), .ok2(calculate_rest_1_ok2), .error(out_15));
  number_splitter number_splitter_3 (
    .num_in(calculate_rest_1_rest), .units_out(number_splitter_3_units_out),
    .tens_out(number_splitter_3_tens_out), .hundreds_out(number_splitter_3_hundreds_out));
  hex_7seg hex_7seg_7 (.hex_in(number_splitter_3_tens_out), .a_b_c_d_e_f_g(hex_7seg_7_a_b_c_d_e_f_g));
  hex_7seg hex_7seg_8 (.hex_in(number_splitter_3_units_out), .a_b_c_d_e_f_g(hex_7seg_8_a_b_c_d_e_f_g));
  hex_7seg hex_7seg_9 (.hex_in(number_splitter_3_hundreds_out), .a_b_c_d_e_f_g(hex_7seg_9_a_b_c_d_e_f_g));
  _7_Segment_Display #(.decimalPoint("false")) u_7_segment_display_7 (
    .g(hex_7seg_9_a_b_c_d_e_f_g[0]), .f(hex_7seg_9_a_b_c_d_e_f_g[1]), .a(hex_7seg_9_a_b_c_d_e_f_g[6]),
    .b(hex_7seg_9_a_b_c_d_e_f_g[5]), .e(hex_7seg_9_a_b_c_d_e_f_g[2]), .d(hex_7seg_9_a_b_c_d_e_f_g[3]),
    .c(hex_7seg_9_a_b_c_d_e_f_g[4]));
  procesare_rest procesare_rest_1 (
    .rest(calculate_rest_1_rest), .ok(calculate_rest_1_ok2), .unu(procesare_rest_1_unu),
    .doi(procesare_rest_1_doi), .cinci(procesare_rest_1_cinci), .zece(procesare_rest_1_zece),
    .dzeci(procesare_rest_1_dzeci), .czeci(procesare_rest_1_czeci), .ok2(procesare_rest_1_ok2));
  _7_Segment_Display #(.decimalPoint("false")) u_7_segment_display_8 (
    .g(hex_7seg_7_a_b_c_d_e_f_g[0]), .f(hex_7seg_7_a_b_c_d_e_f_g[1]), .a(hex_7seg_7_a_b_c_d_e_f_g[6]),
    .b(hex_7seg_7_a_b_c_d_e_f_g[5]), .e(hex_7seg_7_a_b_c_d_e_f_g[2]), .d(hex_7seg_7_a_b_c_d_e_f_g[3]),
    .c(hex_7seg_7_a_b_c_d_e_f_g[4]));
  _7_Segment_Display #(.decimalPoint("false")) u_7_segment_display_9 (
    .g(hex_7seg_8_a_b_c_d_e_f_g[0]), .f(hex_7seg_8_a_b_c_d_e_f_g[1]), .a(hex_7seg_8_a_b_c_d_e_f_g[6]),
    .b(hex_7seg_8_a_b_c_d_e_f_g[5]), .e(hex_7seg_8_a_b_c_d_e_f_g[2]), .d(hex_7seg_8_a_b_c_d_e_f_g[3]),
    .c(hex_7seg_8_a_b_c_d_e_f_g[4]));
  Button button_3 (.out(button_3_out));
  Button button_4 (.out(button_4_out));
  memory_money memory_money_1 (
    .button(button_3_out), .mode(in_1), .we(in_2), .addr(in_3), .unu(procesare_rest_1_unu),
    .doi(procesare_rest_1_doi), .cinci(procesare_rest_1_cinci), .zece(procesare_rest_1_zece),
    .dzeci(procesare_rest_1_dzeci), .czeci(procesare_rest_1_czeci), .din(in_6), .ok(procesare_rest_1_ok2),
    .unu_out(out_8), .doi_out(out_9), .cinci_out(out_10), .zece_out(out_11), .dzeci_out(out_12),
    .czeci_out(out_13), .dout(out_14), .error(memory_money_1_error));
  memory_tickets memory_tickets_1 (
    .button(button_4_out), .numar_bilete(in_7), .ok(procesare_rest_1_ok2), .numar_bilete_out(out_16),
    .error(memory_tickets_1_error));
  LED led_2 (.in(memory_money_1_error));
  LED led_3 (.in(memory_tickets_1_error));
endmodule

// VHDL entity memory_money, as the project stores it:
library ieee;
use ieee.std_logic_1164.all;
use ieee.numeric_std.all;
--use ieee.std_logic_unsigned;
--use ieee.std_logic_arith.all;

entity memory_money is
    port (
        button    : in  std_logic;
        mode      : in  std_logic;-- mode e 0-> admin
        					    -- mode e 1-> user
        we        : in  std_logic;
        addr      : in  std_logic_vector(2 downto 0);
        unu       : in  std_logic_vector(6 downto 0);
        doi       : in  std_logic_vector(6 downto 0);
        cinci     : in  std_logic_vector(6 downto 0);
        zece      : in  std_logic_vector(6 downto 0);
        dzeci     : in  std_logic_vector(6 downto 0);
        czeci     : in  std_logic_vector(6 downto 0);
        din       : in  std_logic_vector(7 downto 0);
        ok        : in  std_logic;
        unu_out   : out std_logic_vector(7 downto 0);
        doi_out   : out std_logic_vector(7 downto 0);
        cinci_out : out std_logic_vector(7 downto 0);
        zece_out  : out std_logic_vector(7 downto 0);
        dzeci_out : out std_logic_vector(7 downto 0);
        czeci_out : out std_logic_vector(7 downto 0);
        dout      : out std_logic_vector(7 downto 0);
        error     : out std_logic
    );
end entity memory_money;

architecture rtl of memory_money is
    type memory_array is array (0 to 5) of std_logic_vector(7 downto 0);
    signal memory : memory_array := (others => "00000000");
begin

    process(button,ok)
    variable flag : std_logic;
    begin
        if rising_edge(button) then
                if mode = '0'  then
                    if we = '1' then
                        memory(to_integer(unsigned(addr))) <= din;
                    else
                        dout <= memory(to_integer(unsigned(addr)));
                     end if;
                elsif mode= '1' then
                if unsigned(memory(0)) >= unsigned(unu) then
                    memory(0) <= std_logic_vector(unsigned(memory(0)) - unsigned(unu));
                else
                    flag := '1';
                end if;
                if unsigned(memory(1)) >= unsigned(doi) and flag /='1' then
                    memory(1) <= std_logic_vector(unsigned(memory(1)) - unsigned(doi));
                 else
                    flag := '1';
                end if;
                if unsigned(memory(2)) >= unsigned(cinci) and flag /='1' then
                    memory(2) <= std_logic_vector(unsigned(memory(2)) - unsigned(cinci));
                else
                    flag := '1';
                end if;
                if unsigned(memory(3)) >= unsigned(zece) and flag /='1'  then
                    memory(3) <= std_logic_vector(unsigned(memory(3)) - unsigned(zece));        
                else
                    flag := '1';
                end if;
                if unsigned(memory(4)) >= unsigned(dzeci) and flag /='1' then
                    memory(4) <= std_logic_vector(unsigned(memory(4)) - unsigned(dzeci));
                else
                    flag := '1';
                end if; 
                if unsigned(memory(5)) >= unsigned(czeci) and flag /='1' then
                    memory(5) <= std_logic_vector(unsigned(memory(5)) - unsigned(czeci));
                else
                    flag := '1';
                end if;
            end if;
            if flag ='1' then
            	error <= '1';
            else
            	error <= '0';
            end if;
            unu_out <= memory(0);
            doi_out <= memory(1);
            cinci_out <= memory(2);
            zece_out <= memory(3);
            dzeci_out <= memory(4);
            czeci_out <= memory(5);
        end if;
    end process;

end rtl;

// VHDL entity calculate_cost, as the project stores it:
library ieee;
use ieee.std_logic_1164.all;
use ieee.numeric_std.all;

entity calculate_cost is
    port (
        button   : in  std_logic;
        data_in  : in  std_logic_vector(5 downto 0);
        data_out : out std_logic_vector(6 downto 0);
        error    : out std_logic
    );
end entity calculate_cost;

architecture rtl of calculate_cost is
    signal shift_reg : std_logic_vector(6 downto 0);
begin
    process(button)
    begin
        if rising_edge(button) then
            if (to_integer(unsigned(data_in)) <= 50) then
                shift_reg <= data_in & '0';  -- Shift left and insert new data at the end
                error <= '0';  -- Reset the error signal
            else
                shift_reg <= (others => '0');  -- Set shift_reg to 0 when data_in > 50
                error <= '1';  -- Set the error signal to 1
            end if;
        end if;
    end process;

    data_out <= shift_reg;
end architecture rtl;

// VHDL entity segment_7, as the project stores it:
LIBRARY ieee;
USE ieee.std_logic_1164.all;
					  
ENTITY segment_7 IS
							
  PORT (
     val           : IN  std_logic_vector(3 DOWNTO 0);
  	a_b_c_d_e_f_g : OUT std_logic_vector(6 downTO 0)
    );
END segment_7;
--   a
--f     b
--   g
--e     c
--   d
--
--
ARCHITECTURE TypeArchitecture OF segment_7 IS

BEGIN
		a_b_c_d_e_f_g <= "0000001" when val = x"0" else
				       "1001111" when val = x"1" else
				       "0010010" when val = x"2" else
				       "0000110" when val = x"3" else
				       "1001100" when val = x"4" else
				       "0100100" when val = x"5" else
				       "0100000" when val = x"6" else
				       "0001111" when val = x"7" else
				       "0000000" when val = x"8" else
				       "0000100" when val = x"9" else
				       "0001000" when val = x"A" else
				       "1100000" when val = x"b" else
				       "1110010" when val = x"c" else
				       "1000010" when val = x"d" else
				       "0110000" when val = x"E" else
				       "0111000" when val = x"F" ;	-- toate segmentele stinse
				       		

END TypeArchitecture;

// VHDL entity number_splitter, as the project stores it:
library ieee;
use ieee.std_logic_1164.all;
use ieee.numeric_std.all;

entity number_splitter is
  port (
    num_in : in std_logic_vector(6 downto 0);
    units_out : out std_logic_vector(3 downto 0);
    tens_out : out std_logic_vector(3 downto 0);
    hundreds_out : out std_logic_vector(3 downto 0)
  );
end entity number_splitter;

architecture behavior of number_splitter is
  signal num : integer;
begin
  num <= to_integer(unsigned(num_in));
  units_out <= std_logic_vector(to_unsigned(num mod 10, 4));
  tens_out <= std_logic_vector(to_unsigned(num / 10 mod 10, 4));
  hundreds_out <= std_logic_vector(to_unsigned(num / 100 mod 10, 4));
end architecture behavior;

// VHDL entity introduce_money, as the project stores it:
library ieee;
use ieee.std_logic_1164.all;
use ieee.numeric_std.all;

entity introduce_money is
    port (
        cost        : in  std_logic_vector(6 downto 0);
        button      : in  std_logic;
        addr        : in  std_logic_vector(2 downto 0);
        suma_data   : out std_logic_vector(6 downto 0);
        suma_ceruta : out std_logic_vector(6 downto 0);
        ok          : out std_logic --cand am ajuns la suma ceruta, trecem la acordarea restului
    );
end entity introduce_money;

architecture rtl of introduce_money is
    signal suma_ceruta_int : integer := 0;
    signal introdus_semnal : integer := 0;
    
begin
    suma_ceruta_int <= to_integer(unsigned(cost));
    suma_ceruta <= cost;
    process(button)
        variable introdus : integer := introdus_semnal;
    begin
        if rising_edge(button) then
            case addr is
                when "000" =>
                    introdus := introdus + 1;
                when "001" =>
                    introdus := introdus + 2;
                when "010" =>
                    introdus := introdus + 5;
                when "011" =>
                    introdus := introdus + 10;
                when "100" =>
                    introdus := introdus + 20;
                when "101" =>
                    introdus := introdus + 50;
                when others =>
                    null;
            end case;
            
            if introdus >= suma_ceruta_int then
                suma_data <= std_logic_vector(to_unsigned(introdus, 7));
                ok <= '1';
            else
            	 ok <= '0';
            end if;
            
            introdus_semnal <= introdus;
        end if;
        
        suma_data <= std_logic_vector(to_unsigned(introdus, 7));
    end process;

end architecture rtl;

// VHDL entity calculate_rest, as the project stores it:
LIBRARY ieee;
USE ieee.std_logic_1164.all;
USE ieee.numeric_std.all;
use ieee.std_logic_unsigned.all;
ENTITY calculate_rest IS
  PORT (
    suma_data   : in std_logic_vector(6 downto 0);
    suma_ceruta : in std_logic_vector(6 downto 0);
    ok          : in std_logic;
    rest        : out std_logic_vector(6 downto 0);
    ok2         : out std_logic;
    error       : out std_logic
    );
END calculate_rest;

ARCHITECTURE TypeArchitecture OF calculate_rest IS
  signal rest_int        : integer;
  signal suma_data_int   : integer;
  signal suma_ceruta_int : integer;
BEGIN
  ok2 <= ok;
  process(ok)
  begin
  if ok ='1' then
    error           <= '0';
    rest <= suma_data-suma_ceruta;
   else
	error <= '1';
   end if;
  end process;
  
END TypeArchitecture;

// VHDL entity procesare_rest, as the project stores it:
LIBRARY ieee;
USE ieee.std_logic_1164.all;

use ieee.numeric_std.all;

ENTITY procesare_rest IS
  PORT (
  	rest   : in std_logic_vector(6 downto 0);
  	ok     : in std_logic;
  	unu    : out std_logic_vector(6 downto 0);
  	doi    : out std_logic_vector(6 downto 0);
  	cinci  : out std_logic_vector(6 downto 0);
  	zece   : out std_logic_vector(6 downto 0);
  	dzeci  : out std_logic_vector(6 downto 0);
  	czeci  : out std_logic_vector(6 downto 0);
  	ok2    : out std_logic
    );
END procesare_rest;
            
ARCHITECTURE TypeArchitecture OF procesare_rest IS
	signal left : natural :=0 ;
BEGIN
	ok2 <= ok;
     left <= to_integer(unsigned(rest));

	process(ok,left)
     variable ramas : natural;
     variable unu_int : natural := 0;
     variable doi_int : natural := 0;
     variable cinci_int : natural := 0;
     variable zece_int : natural := 0;
     variable dzeci_int : natural := 0;
     variable czeci_int : natural := 0;
	begin
		if ok = '1' then
		ramas := left;
		czeci_int:=ramas/50;
		czeci<=std_logic_vector(to_unsigned(czeci_int,7));
		ramas:=ramas-czeci_int*50;
		dzeci_int:=ramas/20;
		dzeci<=std_logic_vector(to_unsigned(dzeci_int,7));
		ramas:=ramas-dzeci_int*20;
		zece_int:=ramas/10;
		zece<=std_logic_vector(to_unsigned(zece_int,7));
		ramas:=ramas-zece_int*10;
		cinci_int:=ramas/5;
		cinci<=std_logic_vector(to_unsigned(cinci_int,7));
		ramas:=ramas-cinci_int*5;
		doi_int:=ramas/2;
		doi<=std_logic_vector(to_unsigned(doi_int,7));
		ramas:=ramas-doi_int*2;
		unu_int:=ramas;
		unu<=std_logic_vector(to_unsigned(unu_int,7));
		end if;
	end process;
	
END TypeArchitecture;

// VHDL entity memory_tickets, as the project stores it:
library ieee;
use ieee.std_logic_1164.all;
use ieee.numeric_std.all;

entity memory_tickets is
    port (
    button           : in std_logic;
    numar_bilete 	  : in std_logic_vector(6 downto 0);
    ok 			  : in std_logic;
    numar_bilete_out : out std_logic_vector(6 downto 0);
    error            : out std_logic
    );
end entity memory_tickets;

architecture Behavioral of memory_tickets is
    signal nr_bilete : unsigned(6 downto 0);
begin
    process (button,ok)
    begin
    if rising_edge(button) then
        if ok = '1' then
        	if unsigned(numar_bilete) > 0 then
            nr_bilete <= unsigned(numar_bilete) - 1;
            error <= '0';
          else
           error <= '1';
          end if;
        else
        	  nr_bilete <= unsigned(numar_bilete);
        end if;
     end if;
    end process;

    numar_bilete_out <= std_logic_vector(nr_bilete);
end architecture Behavioral;

// VHDL entity hex_7seg, as the project stores it:
LIBRARY ieee;
USE ieee.std_logic_1164.all;

ENTITY hex_7seg IS

  PORT (
 		hex_in: in std_logic_vector(3 downto 0);
  		a_b_c_d_e_f_g: out std_logic_vector(6 downto 0)
  		);

END hex_7seg;

ARCHITECTURE arch_hex OF hex_7seg IS

BEGIN

	a_b_c_d_e_f_g <= "1111110" when hex_in= x"0" else
				  "0110000" when hex_in= x"1" else
				  "1101101" when hex_in= x"2" else
				  "1111001" when hex_in= x"3" else
				  "0110011" when hex_in= x"4" else
				  "1011011" when hex_in= x"5" else
				  "1011111" when hex_in= x"6" else
				  "1110000" when hex_in= x"7" else
				  "1111111" when hex_in= x"8" else
				  "1111011" when hex_in= x"9" else
				  "1110111" when hex_in= x"A" else
				  "0011111" when hex_in= x"B" else
				  "1001110" when hex_in= x"C" else
				  "0111101" when hex_in= x"d" else
				  "1001111" when hex_in= x"E" else
				  "0000001" when hex_in= x"F" else
				  "0000000";

END arch_hex;
